# Fritzing sketch Moisture Sensor (saved by Fritzing 0.9.4)
breadboards: 1

parts:
  Chirp!_Soil_Moisture_Sensor1 = Chirp! Soil Moisture Sensor v2.7.3
  Argon1 = Particle Argon
  Grove1 = Grove OLED 128x96  # not connected

nets:
  N1: Chirp!_Soil_Moisture_Sensor1.Pin_1, Argon1.A2
  N2: Chirp!_Soil_Moisture_Sensor1.pin_3, Argon1.A0, Argon1.SDA, Argon1.SCL

custom parts:
  Particle Argon: The Argon is a powerful Wi-Fi enabled development board that can act as either a standalone Wi-Fi endpoint or Wi-Fi enabled gateway for Particle Mesh networks. It is based on the Nordic nRF52840 and has built-in battery charging circuitry so it’s easy to connect a Li-Po and deploy your local network in minutes. The Argon is great for connecting existing projects to the Particle Device Cloud or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
