# Fritzing sketch MoistureThisOneiscorrect (saved by Fritzing 0.9.4)
breadboards: 1

parts:
  Argon1 = Particle Argon
  SENS1 = SoilWatch 10
  Grove1 = Grove OLED 128x96

nets:
  VCC: Argon1.3.3V, SENS1.VCC, SENS1.OUT, Grove1.VCC
  N1: Argon1.A4, SENS1.GND
  N2: Argon1.SDA, Grove1.SDA
  N3: Argon1.SCL, Grove1.SCL

custom parts:
  Particle Argon: The Argon is a powerful Wi-Fi enabled development board that can act as either a standalone Wi-Fi endpoint or Wi-Fi enabled gateway for Particle Mesh networks. It is based on the Nordic nRF52840 and has built-in battery charging circuitry so it’s easy to connect a Li-Po and deploy your local network in minutes. The Argon is great for connecting existing projects to the Particle Device Cloud or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
  SoilWatch 10: SoilWatch 10 - Capacitive soil moisture sensor
